# Fritzing sketch DIAGRAMAELETRICOassistente (saved by Fritzing 0.9.5d)
breadboards: 1

parts:
  U1 = LIPO-110mAh [package=lipo-110]
  TP1 = TP4056 [chip_label=TP4056 package="DIP (Dual Inline) [THT]"]
  MOD1 = MT3608 Boost No usb
  S3 = SWITCH-DPDT-latching [package=os]
  Componente1 = Arduino Uno (Rev3)
  DFRobot_DFPlayer_Mini1 = DFRobot DFPlayer Mini [part_number=DFR0299]
  SP1 = SPEAKER [package=pcb_mount_speaker]
  S4 = SWITCH-DPDT-latching [package=os]
  S5 = SWITCH-DPDT-latching [package=os]
  S6 = SWITCH-DPDT-latching [package=os]
  S7 = SWITCH-DPDT-latching [package=os]
  S8 = SWITCH-DPDT-latching [package=os]
  S9 = Toggle Switch [package=THT]
  S10 = Momentary Switch [package=ksa_sealed_tac_switch]
  S12 = Toggle Switch [package=THT]
  R1 = Resistor [tolerance=±20% resistance=1000 package=THT]
  C1 = Electrolytic Capacitor [capacitance=1µF package="100 mil [THT, electrolytic]"]

nets:
  N1: U1.+, TP1.pin4, S12.COM
  N2: U1.-, TP1.pin5
  N3: TP1.pin3, MOD1.IN_(+), S12.L1
  N4: TP1.pin6, MOD1.IN_(-), MOD1.OUT_(-), S3.2, Componente1.GND, S4.2, S5.2, S6.2, S7.2, S8.2, S9.COM, S10.2, C1.-
  VIN: MOD1.OUT_(+), Componente1.VIN, DFRobot_DFPlayer_Mini1.VCC
  N5: Componente1.D8, S8.1
  N6: Componente1.D9_PWM, S7.1
  N7: Componente1.D10_PWM/SS, S6.1
  N8: Componente1.D11_PWM/MOSI, S5.1
  N9: Componente1.D12/MISO, S4.1
  N10: Componente1.D0/RX, DFRobot_DFPlayer_Mini1.TX
  N11: Componente1.D1/TX, R1.Pin_0
  N12: Componente1.D5_PWM, DFRobot_DFPlayer_Mini1.BUSY
  N13: Componente1.D6_PWM, S9.L1
  N14: Componente1.D7, S10.1
  N15: DFRobot_DFPlayer_Mini1.RX, R1.Pin_1
  N16: DFRobot_DFPlayer_Mini1.SPK_1, SP1.+
  N17: DFRobot_DFPlayer_Mini1.SPK_2, SP1.-

custom parts:
  TP4056: A DIP stand-in part for whatever IC you want. With 6 pins on a 300mil dual inline package (DIP) footprint.
  MT3608 Boost No usb: Chip- MT3608 / B6289 DC to DC step up, power booster module. With adjustable output voltage. Current- 2A . || Input voltage- 2V-24V || Output voltage- 5V-28V Input interface- Inversed polarity- NO. || Led indicator- No.
  SWITCH-DPDT-latching: DPDT latching pushbutton switch
